// Logisim project imm-gen.circ as structural Verilog: 1 circuit, main circuit imm_gen
module imm_gen (
  input  [31:0] Instruction,
  input  [2:0] ImmSel,
  output [31:0] Immediate
);

  wire [31:0] csr5, i0;
  wire [31:5] s1;
  wire [31:12] b2;
  wire [31:20] j4;

  assign b2 = {{19{Instruction[31]}}, Instruction[31]};  // Bit_Extender bit_extender_1
  assign j4 = {{11{Instruction[31]}}, Instruction[31]};  // Bit_Extender bit_extender_2
  assign csr5 = {{27{Instruction[19]}}, Instruction[19:15]};  // Bit_Extender bit_extender_3
  assign i0 = {{20{Instruction[31]}}, Instruction[31:20]};  // Bit_Extender bit_extender_4
  assign s1 = {{20{Instruction[31]}}, Instruction[31:25]};  // Bit_Extender bit_extender_5
  Multiplexer #(.enable("false"), .select(3), .width(32)) multiplexer_1 (
    .in0(i0), .in1({s1, Instruction[11:7]}),
    .in2({b2, Instruction[7], Instruction[30:25], Instruction[11:8], 1'b0}),
    .in3({Instruction[31:12], {12{1'b0}}}),
    .in4({j4, Instruction[19:12], Instruction[20], Instruction[30:21], 1'b0}), .in5(csr5), .out(Immediate),
    .sel(ImmSel));  // open: in6, in7

  // Other names for the same wires on the sheet: b2[11:1] = {Instruction[7], Instruction[30:25], Instruction[11:8]};
  //   s1[4:0] = Instruction[11:7]; j4[19:1] = {Instruction[19:12], Instruction[20], Instruction[30:21]};
  //   u3[31:12] = Instruction[31:12]

  // Notes on the sheet:
  //   INPUTS to your circuit
  //   DON'T CHANGE THE LOCATIONS OF THE INPUTS AND OUTPUTS!
  //   OUTPUT from your circuit
endmodule
