// Logisim project regfile.circ as structural Verilog: 1 circuit, main circuit regfile
module regfile (
  input  [4:0] ReadReg1,
  input  [4:0] ReadReg2,
  input  [4:0] WriteReg,
  input  [31:0] RegWriteData,
  input  RegWEn,
  input  clk,
  output [31:0] ra,
  output [31:0] sp,
  output [31:0] t0,
  output [31:0] t1,
  output [31:0] t2,
  output [31:0] s0,
  output [31:0] s1,
  output [31:0] a0,
  output [31:0] RegReadData1,
  output [31:0] RegReadData2
);

  wire x1regw, x2regw, x3regw, x4regw, x5regw, x6regw, x7regw, x8regw, x9regw, x10regw, x11regw, x12regw,
       x13regw, x14regw, x15regw, x16regw, x17regw, x18regw, x19regw, x20regw, x21regw, x22regw, x23regw,
       x24regw, x25regw, x26regw, x27regw, x28regw, x29regw, x30regw, x31regw;
  wire [31:0] x0, x3, x4, x11, x12, x13, x14, x15, x16, x17, x18, x19, x20, x21, x22, x23, x24, x25, x26,
       x27, x28, x29, x30, x31;

  Demultiplexer #(.enable("false"), .select(5)) demultiplexer_1 (
    .out1(x1regw), .out2(x2regw), .out3(x3regw), .out4(x4regw), .out5(x5regw), .out6(x6regw), .out7(x7regw),
    .out8(x8regw), .out9(x9regw), .out10(x10regw), .out11(x11regw), .out12(x12regw), .out13(x13regw),
    .out14(x14regw), .out15(x15regw), .out16(x16regw), .out17(x17regw), .out18(x18regw), .out19(x19regw),
    .out20(x20regw), .out21(x21regw), .out22(x22regw), .out23(x23regw), .out24(x24regw), .out25(x25regw),
    .out26(x26regw), .out27(x27regw), .out28(x28regw), .out29(x29regw), .out30(x30regw), .out31(x31regw),
    .in(RegWEn), .sel(WriteReg));  // open: out0
  Register #(.width(32)) register_1 (.D(RegWriteData), .clk(clk), .Q(x0), .clr(1'b1));  // open: en
  Register #(.width(32)) register_2 (.D(RegWriteData), .en(x6regw), .clk(clk), .Q(t1));  // open: clr
  Register #(.width(32)) register_3 (.D(RegWriteData), .en(x12regw), .clk(clk), .Q(x12));  // open: clr
  Register #(.width(32)) register_4 (.D(RegWriteData), .en(x18regw), .clk(clk), .Q(x18));  // open: clr
  Register #(.width(32)) register_5 (.D(RegWriteData), .en(x24regw), .clk(clk), .Q(x24));  // open: clr
  Register #(.width(32)) register_6 (.D(RegWriteData), .en(x30regw), .clk(clk), .Q(x30));  // open: clr
  Register #(.width(32)) register_7 (.D(RegWriteData), .en(x1regw), .clk(clk), .Q(ra));  // open: clr
  Register #(.width(32)) register_8 (.D(RegWriteData), .en(x7regw), .clk(clk), .Q(t2));  // open: clr
  Register #(.width(32)) register_9 (.D(RegWriteData), .en(x13regw), .clk(clk), .Q(x13));  // open: clr
  Register #(.width(32)) register_10 (.D(RegWriteData), .en(x19regw), .clk(clk), .Q(x19));  // open: clr
  Register #(.width(32)) register_11 (.D(RegWriteData), .en(x25regw), .clk(clk), .Q(x25));  // open: clr
  Register #(.width(32)) register_12 (.D(RegWriteData), .en(x31regw), .clk(clk), .Q(x31));  // open: clr
  Multiplexer #(.enable("false"), .select(5), .width(32)) multiplexer_1 (
    .in0(x0), .in1(ra), .in2(sp), .in3(x3), .in4(x4), .in5(t0), .in6(t1), .in7(t2), .in8(s0), .in9(s1),
    .in10(a0), .in11(x11), .in12(x12), .in13(x13), .in14(x14), .in15(x15), .in16(x16), .in17(x17),
    .in18(x18), .in19(x19), .in20(x20), .in21(x21), .in22(x22), .in23(x23), .in24(x24), .in25(x25),
    .in26(x26), .in27(x27), .in28(x28), .in29(x29), .in30(x30), .in31(x31), .out(RegReadData1), .sel(ReadReg1));
  Register #(.width(32)) register_13 (.D(RegWriteData), .en(x2regw), .clk(clk), .Q(sp));  // open: clr
  Register #(.width(32)) register_14 (.D(RegWriteData), .en(x8regw), .clk(clk), .Q(s0));  // open: clr
  Register #(.width(32)) register_15 (.D(RegWriteData), .en(x14regw), .clk(clk), .Q(x14));  // open: clr
  Register #(.width(32)) register_16 (.D(RegWriteData), .en(x20regw), .clk(clk), .Q(x20));  // open: clr
  Register #(.width(32)) register_17 (.D(RegWriteData), .en(x26regw), .clk(clk), .Q(x26));  // open: clr
  Register #(.width(32)) register_18 (.D(RegWriteData), .en(x3regw), .clk(clk), .Q(x3));  // open: clr
  Register #(.width(32)) register_19 (.D(RegWriteData), .en(x9regw), .clk(clk), .Q(s1));  // open: clr
  Register #(.width(32)) register_20 (.D(RegWriteData), .en(x15regw), .clk(clk), .Q(x15));  // open: clr
  Register #(.width(32)) register_21 (.D(RegWriteData), .en(x21regw), .clk(clk), .Q(x21));  // open: clr
  Register #(.width(32)) register_22 (.D(RegWriteData), .en(x27regw), .clk(clk), .Q(x27));  // open: clr
  Register #(.width(32)) register_23 (.D(RegWriteData), .en(x4regw), .clk(clk), .Q(x4));  // open: clr
  Register #(.width(32)) register_24 (.D(RegWriteData), .en(x10regw), .clk(clk), .Q(a0));  // open: clr
  Register #(.width(32)) register_25 (.D(RegWriteData), .en(x16regw), .clk(clk), .Q(x16));  // open: clr
  Register #(.width(32)) register_26 (.D(RegWriteData), .en(x22regw), .clk(clk), .Q(x22));  // open: clr
  Register #(.width(32)) register_27 (.D(RegWriteData), .en(x28regw), .clk(clk), .Q(x28));  // open: clr
  Register #(.width(32)) register_28 (.D(RegWriteData), .en(x5regw), .clk(clk), .Q(t0));  // open: clr
  Register #(.width(32)) register_29 (.D(RegWriteData), .en(x11regw), .clk(clk), .Q(x11));  // open: clr
  Register #(.width(32)) register_30 (.D(RegWriteData), .en(x17regw), .clk(clk), .Q(x17));  // open: clr
  Register #(.width(32)) register_31 (.D(RegWriteData), .en(x23regw), .clk(clk), .Q(x23));  // open: clr
  Register #(.width(32)) register_32 (.D(RegWriteData), .en(x29regw), .clk(clk), .Q(x29));  // open: clr
  Multiplexer #(.enable("false"), .select(5), .width(32)) multiplexer_2 (
    .in0(x0), .in1(ra), .in2(sp), .in3(x3), .in4(x4), .in5(t0), .in6(t1), .in7(t2), .in8(s0), .in9(s1),
    .in10(a0), .in11(x11), .in12(x12), .in13(x13), .in14(x14), .in15(x15), .in16(x16), .in17(x17),
    .in18(x18), .in19(x19), .in20(x20), .in21(x21), .in22(x22), .in23(x23), .in24(x24), .in25(x25),
    .in26(x26), .in27(x27), .in28(x28), .in29(x29), .in30(x30), .in31(x31), .out(RegReadData2), .sel(ReadReg2));

  // Notes on the sheet:
  //   INPUTS to your circuit
  //   DON'T CHANGE THE LOCATIONS OF THE INPUTS AND OUTPUTS!
  //   These are DEBUG/TEST outputs from your circuit.
  //   OUTPUTS from your circuit
endmodule
